# Fritzing sketch screenNumberBoard (saved by Fritzing 0.9.9b)
perfboards: 1

parts:
  J4 = female pin header, 7 pins [form="♀ (female)"]
  J5 = female pin header, 7 pins [form="♀ (female)"]
  Composant1 = Arduino Uno (Rev3)
  J2 = female pin header, 4 pins [form="♀ (female)"]
  J6 = female pin header, 8 pins [form="♀ (female)"]
  R1 = Resistor [tolerance=±5% resistance=1k package=THT]
  R2 = Resistor [tolerance=±5% resistance=1k package=THT]
  R3 = Resistor [tolerance=±5% resistance=1k package=THT]
  R4 = Resistor [tolerance=±5% resistance=1k package=THT]
  J7 = female pin header, 2 pins [form="♀ (female)"]
  R5 = Resistor [tolerance=±5% resistance=1k package=THT]

nets:
  N1: J4.pin1, R4.Pin_1
  N2: J4.pin2, Composant1.D9_PWM, J6.pin8
  N3: J4.pin3, Composant1.D4
  N4: J4.pin4, R3.Pin_1
  N5: J4.pin5, R2.Pin_1
  N6: J4.pin6, Composant1.D8, J6.pin7
  N7: J4.pin7, J7.pin2
  N8: J5.pin1, Composant1.D5_PWM, J6.pin4
  N9: J5.pin2, Composant1.D6_PWM, J6.pin5
  N10: J5.pin3, Composant1.D2, J6.pin1
  N11: J5.pin4, Composant1.D7, J6.pin6
  N12: J5.pin5, Composant1.D3_PWM
  N13: J5.pin6, R1.Pin_1
  N14: J5.pin7, R5.Pin_1
  N15: Composant1.D10_PWM/SS, J2.pin1
  N16: Composant1.D11_PWM/MOSI, J2.pin2
  N17: Composant1.D12/MISO, J2.pin3
  N18: Composant1.D13/SCK, J2.pin4
  N19: J7.pin1, R5.Pin_0

notes:
  Numbering (from top to bottom) :
  - Digit : 1 to 4
  - Segment : a to g
  To control : from display
  Digit : || Segment :
