# Fritzing sketch test_draw (saved by Fritzing 0.9.9b)
breadboards: 1

parts:
  Composant1 = Arduino Uno (Rev3)
  R1 = Resistor [tolerance=±5% resistance=220 package=THT]
  LED1 = LED - 5mm [color="Red (633nm)" package="5 mm [THT]"]

nets:
  N1: Composant1.5V, R1.Pin_0
  N2: R1.Pin_1, LED1.cathode
